// Logisim project Clock project.circ as structural Verilog: 12 circuits, main circuit main
module main (
);

  wire clock_1_out, hour_1_hour_lsb_left, hour_1_hour_lsb_right, hour_1_hour_msb_left, hour_1_hour_msb_right,
       hour_1_out_3, hour_1_out_4, hour_1_out_7, hour_1_out_8, minute_1_clock_pulse_for_hour,
       minute_1_minute_right_lsb, minute_1_minute_right_lsb_2, minute_1_minute_right_msb,
       minute_1_minute_right_msb_2, minute_1_out_3, minute_1_out_4, minute_1_out_7, minute_1_out_8,
       n7_segment_1_a, n7_segment_1_b, n7_segment_1_c, n7_segment_1_d, n7_segment_1_e, n7_segment_1_f,
       n7_segment_1_g, n7_segment_2_a, n7_segment_2_b, n7_segment_2_c, n7_segment_2_d, n7_segment_2_e,
       n7_segment_2_f, n7_segment_2_g, n7_segment_3_a, n7_segment_3_b, n7_segment_3_c, n7_segment_3_d,
       n7_segment_3_e, n7_segment_3_f, n7_segment_3_g, n7_segment_4_a, n7_segment_4_b, n7_segment_4_c,
       n7_segment_4_d, n7_segment_4_e, n7_segment_4_f, n7_segment_4_g, n7_segment_5_a, n7_segment_5_b,
       n7_segment_5_c, n7_segment_5_d, n7_segment_5_e, n7_segment_5_f, n7_segment_5_g, n7_segment_6_a,
       n7_segment_6_b, n7_segment_6_c, n7_segment_6_d, n7_segment_6_e, n7_segment_6_f, n7_segment_6_g,
       second_1_clock_pulse_for_minjte, second_1_out_3, second_1_out_4, second_1_out_7, second_1_out_8,
       second_1_second_right_lsb, second_1_second_right_lsb_2, second_1_second_right_msb,
       second_1_second_right_msb_2;

  Clock clock_1 (.out(clock_1_out));
  second second_1 (
    .clock(clock_1_out), .clock_pulse_for_minjte(second_1_clock_pulse_for_minjte),
    .second_right_lsb(second_1_second_right_lsb), .out_3(second_1_out_3), .out_4(second_1_out_4),
    .second_right_msb(second_1_second_right_msb), .second_right_lsb_2(second_1_second_right_lsb_2),
    .out_7(second_1_out_7), .out_8(second_1_out_8), .second_right_msb_2(second_1_second_right_msb_2));
  minute minute_1 (
    .clock(second_1_clock_pulse_for_minjte), .clock_pulse_for_hour(minute_1_clock_pulse_for_hour),
    .minute_right_lsb(minute_1_minute_right_lsb), .out_3(minute_1_out_3), .out_4(minute_1_out_4),
    .minute_right_msb(minute_1_minute_right_msb), .minute_right_lsb_2(minute_1_minute_right_lsb_2),
    .out_7(minute_1_out_7), .out_8(minute_1_out_8), .minute_right_msb_2(minute_1_minute_right_msb_2));
  hour hour_1 (
    .in_1(minute_1_clock_pulse_for_hour), .hour_lsb_right(hour_1_hour_lsb_right), .out_3(hour_1_out_3),
    .out_4(hour_1_out_4), .hour_msb_right(hour_1_hour_msb_right), .hour_lsb_left(hour_1_hour_lsb_left),
    .out_7(hour_1_out_7), .out_8(hour_1_out_8), .hour_msb_left(hour_1_hour_msb_left));
  _7_Segment u_7_segment_1 (
    .in_1(second_1_second_right_lsb), .in_2(second_1_out_3), .in_3(second_1_out_4),
    .in_4(second_1_second_right_msb), .A(n7_segment_1_a), .B(n7_segment_1_b), .C(n7_segment_1_c),
    .D(n7_segment_1_d), .E(n7_segment_1_e), .F(n7_segment_1_f), .G(n7_segment_1_g));
  _7_Segment u_7_segment_2 (
    .in_1(second_1_second_right_lsb_2), .in_2(second_1_out_7), .in_3(second_1_out_8),
    .in_4(second_1_second_right_msb_2), .A(n7_segment_2_a), .B(n7_segment_2_b), .C(n7_segment_2_c),
    .D(n7_segment_2_d), .E(n7_segment_2_e), .F(n7_segment_2_f), .G(n7_segment_2_g));
  _7_Segment u_7_segment_3 (
    .in_1(minute_1_minute_right_lsb), .in_2(minute_1_out_3), .in_3(minute_1_out_4),
    .in_4(minute_1_minute_right_msb), .A(n7_segment_3_a), .B(n7_segment_3_b), .C(n7_segment_3_c),
    .D(n7_segment_3_d), .E(n7_segment_3_e), .F(n7_segment_3_f), .G(n7_segment_3_g));
  _7_Segment u_7_segment_4 (
    .in_1(minute_1_minute_right_lsb_2), .in_2(minute_1_out_7), .in_3(minute_1_out_8),
    .in_4(minute_1_minute_right_msb_2), .A(n7_segment_4_a), .B(n7_segment_4_b), .C(n7_segment_4_c),
    .D(n7_segment_4_d), .E(n7_segment_4_e), .F(n7_segment_4_f), .G(n7_segment_4_g));
  _7_Segment u_7_segment_5 (
    .in_1(hour_1_hour_lsb_right), .in_2(hour_1_out_3), .in_3(hour_1_out_4), .in_4(hour_1_hour_msb_right),
    .A(n7_segment_5_a), .B(n7_segment_5_b), .C(n7_segment_5_c), .D(n7_segment_5_d), .E(n7_segment_5_e),
    .F(n7_segment_5_f), .G(n7_segment_5_g));
  _7_Segment u_7_segment_6 (
    .in_1(hour_1_hour_lsb_left), .in_2(hour_1_out_7), .in_3(hour_1_out_8), .in_4(hour_1_hour_msb_left),
    .A(n7_segment_6_a), .B(n7_segment_6_b), .C(n7_segment_6_c), .D(n7_segment_6_d), .E(n7_segment_6_e),
    .F(n7_segment_6_f), .G(n7_segment_6_g));
  _7_Segment_Display u_7_segment_display_1 (
    .g(n7_segment_6_g), .f(n7_segment_6_f), .a(n7_segment_6_a), .b(n7_segment_6_b), .e(n7_segment_6_e),
    .d(n7_segment_6_d), .c(n7_segment_6_c));  // open: dp
  _7_Segment_Display u_7_segment_display_2 (
    .g(n7_segment_5_g), .f(n7_segment_5_f), .a(n7_segment_5_a), .b(n7_segment_5_b), .e(n7_segment_5_e),
    .d(n7_segment_5_d), .c(n7_segment_5_c));  // open: dp
  _7_Segment_Display u_7_segment_display_3 (
    .g(n7_segment_4_g), .f(n7_segment_4_f), .a(n7_segment_4_a), .b(n7_segment_4_b), .e(n7_segment_4_e),
    .d(n7_segment_4_d), .c(n7_segment_4_c));  // open: dp
  _7_Segment_Display u_7_segment_display_4 (
    .g(n7_segment_3_g), .f(n7_segment_3_f), .a(n7_segment_3_a), .b(n7_segment_3_b), .e(n7_segment_3_e),
    .d(n7_segment_3_d), .c(n7_segment_3_c));  // open: dp
  _7_Segment_Display u_7_segment_display_5 (
    .g(n7_segment_2_g), .f(n7_segment_2_f), .a(n7_segment_2_a), .b(n7_segment_2_b), .e(n7_segment_2_e),
    .d(n7_segment_2_d), .c(n7_segment_2_c));  // open: dp
  _7_Segment_Display u_7_segment_display_6 (
    .g(n7_segment_1_g), .f(n7_segment_1_f), .a(n7_segment_1_a), .b(n7_segment_1_b), .e(n7_segment_1_e),
    .d(n7_segment_1_d), .c(n7_segment_1_c));  // open: dp

  // Notes on the sheet:
  //   2107080
  //   2107079
endmodule

module second (
  input  clock,
  output second_right_lsb,
  output out_3,
  output out_4,
  output second_right_msb,
  output second_right_lsb_2,
  output out_7,
  output out_8,
  output second_right_msb_2,
  output clock_pulse_for_minjte
);

  wire and_1_out, and_2_out, and_4_out, and_5_out, and_6_out, and_7_out, not_1_out, not_2_out, not_3_out,
       not_4_out, not_5_out, not_6_out, not_7_out, not_8_out, not_9_out, not_10_out, not_11_out;

  and and_1 (and_1_out, not_1_out, not_2_out, not_3_out, not_7_out, not_9_out, not_10_out, out_8, not_4_out);
  not not_1 (not_1_out, second_right_msb);
  not not_2 (not_2_out, out_4);
  T_Flip_Flop #(.trigger("falling")) t_ff_1 (
    .clk(clock), .T(1'b1), .Q(second_right_msb), .preset(and_1_out), .reset(and_2_out));  // open: Qn, en
  and and_2 (and_2_out, not_5_out, out_4, not_8_out, second_right_lsb);
  not not_3 (not_3_out, out_3);
  not not_4 (not_4_out, second_right_msb_2);
  T_Flip_Flop #(.trigger("falling")) t_ff_2 (
    .clk(and_2_out), .T(1'b1), .Q(second_right_msb_2), .reset(clock_pulse_for_minjte));  // open: Qn, preset, en
  and and_3 (clock_pulse_for_minjte, not_6_out, out_8, out_7, not_11_out);
  not not_5 (not_5_out, second_right_msb);
  not not_6 (not_6_out, second_right_msb_2);
  not not_7 (not_7_out, second_right_lsb);
  T_Flip_Flop #(.trigger("falling")) t_ff_3 (
    .clk(clock), .T(second_right_msb), .Q(out_4), .reset(and_2_out));  // open: Qn, preset, en
  T_Flip_Flop #(.trigger("falling")) t_ff_4 (
    .clk(and_2_out), .T(second_right_msb_2), .Q(out_8), .reset(clock_pulse_for_minjte));  // open: Qn, preset, en
  and and_4 (and_4_out, out_4, second_right_msb);
  and and_5 (and_5_out, out_8, second_right_msb_2);
  T_Flip_Flop #(.trigger("falling")) t_ff_5 (
    .clk(clock), .T(and_4_out), .Q(out_3), .reset(and_2_out));  // open: Qn, preset, en
  not not_8 (not_8_out, out_3);
  not not_9 (not_9_out, out_7);
  T_Flip_Flop #(.trigger("falling")) t_ff_6 (
    .clk(and_2_out), .T(and_5_out), .Q(out_7), .reset(clock_pulse_for_minjte));  // open: Qn, preset, en
  and and_6 (and_6_out, out_3, and_4_out);
  not not_10 (not_10_out, second_right_lsb_2);
  and and_7 (and_7_out, out_7, and_5_out);
  T_Flip_Flop #(.trigger("falling")) t_ff_7 (
    .clk(clock), .T(and_6_out), .Q(second_right_lsb), .reset(and_2_out));  // open: Qn, preset, en
  T_Flip_Flop #(.trigger("falling")) t_ff_8 (
    .clk(and_2_out), .T(and_7_out), .Q(second_right_lsb_2), .reset(clock_pulse_for_minjte));  // open: Qn, preset, en
  not not_11 (not_11_out, second_right_lsb_2);

  // Notes on the sheet:
  //   2107079
endmodule

module minute (
  input  clock,
  output minute_right_lsb,
  output out_3,
  output out_4,
  output minute_right_msb,
  output minute_right_lsb_2,
  output out_7,
  output out_8,
  output minute_right_msb_2,
  output clock_pulse_for_hour
);

  wire and_1_out, and_2_out, and_4_out, and_5_out, and_6_out, and_7_out, not_1_out, not_2_out, not_3_out,
       not_4_out, not_5_out, not_6_out, not_7_out, not_8_out, not_9_out, not_10_out, not_11_out;

  and and_1 (and_1_out, not_1_out, not_2_out, not_3_out, not_7_out, not_9_out, not_10_out, out_8, not_4_out);
  not not_1 (not_1_out, minute_right_msb);
  not not_2 (not_2_out, out_4);
  T_Flip_Flop #(.trigger("falling")) t_ff_1 (
    .clk(clock), .T(1'b1), .Q(minute_right_msb), .preset(and_1_out), .reset(and_2_out));  // open: Qn, en
  and and_2 (and_2_out, not_5_out, out_4, not_8_out, minute_right_lsb);
  not not_3 (not_3_out, out_3);
  not not_4 (not_4_out, minute_right_msb_2);
  T_Flip_Flop #(.trigger("falling")) t_ff_2 (
    .clk(and_2_out), .T(1'b1), .Q(minute_right_msb_2), .reset(clock_pulse_for_hour));  // open: Qn, preset, en
  and and_3 (clock_pulse_for_hour, not_6_out, out_8, out_7, not_11_out);
  not not_5 (not_5_out, minute_right_msb);
  not not_6 (not_6_out, minute_right_msb_2);
  not not_7 (not_7_out, minute_right_lsb);
  T_Flip_Flop #(.trigger("falling")) t_ff_3 (
    .clk(clock), .T(minute_right_msb), .Q(out_4), .reset(and_2_out));  // open: Qn, preset, en
  T_Flip_Flop #(.trigger("falling")) t_ff_4 (
    .clk(and_2_out), .T(minute_right_msb_2), .Q(out_8), .reset(clock_pulse_for_hour));  // open: Qn, preset, en
  and and_4 (and_4_out, out_4, minute_right_msb);
  and and_5 (and_5_out, out_8, minute_right_msb_2);
  T_Flip_Flop #(.trigger("falling")) t_ff_5 (
    .clk(clock), .T(and_4_out), .Q(out_3), .reset(and_2_out));  // open: Qn, preset, en
  not not_8 (not_8_out, out_3);
  not not_9 (not_9_out, out_7);
  T_Flip_Flop #(.trigger("falling")) t_ff_6 (
    .clk(and_2_out), .T(and_5_out), .Q(out_7), .reset(clock_pulse_for_hour));  // open: Qn, preset, en
  and and_6 (and_6_out, out_3, and_4_out);
  not not_10 (not_10_out, minute_right_lsb_2);
  and and_7 (and_7_out, out_7, and_5_out);
  T_Flip_Flop #(.trigger("falling")) t_ff_7 (
    .clk(clock), .T(and_6_out), .Q(minute_right_lsb), .reset(and_2_out));  // open: Qn, preset, en
  T_Flip_Flop #(.trigger("falling")) t_ff_8 (
    .clk(and_2_out), .T(and_7_out), .Q(minute_right_lsb_2), .reset(clock_pulse_for_hour));  // open: Qn, preset, en
  not not_11 (not_11_out, minute_right_lsb_2);

  // Notes on the sheet:
  //   2107079
endmodule

module hour (
  input  in_1,
  output hour_lsb_right,
  output out_3,
  output out_4,
  output hour_msb_right,
  output hour_lsb_left,
  output out_7,
  output out_8,
  output hour_msb_left
);

  wire and_1_out, and_2_out, and_3_out, and_4_out, and_5_out, and_6_out, and_7_out, not_1_out, not_2_out,
       not_3_out, not_4_out, not_5_out, not_6_out, not_7_out, not_8_out, not_9_out, not_10_out, or_1_out,
       or_2_out, or_3_out;

  and and_1 (and_1_out, not_1_out, out_4, not_6_out, hour_lsb_right);
  and and_2 (and_2_out, not_2_out, out_8, out_7, not_8_out);
  T_Flip_Flop #(.trigger("falling")) t_ff_1 (
    .clk(in_1), .T(1'b1), .Q(hour_msb_right), .reset(or_1_out));  // open: Qn, preset, en
  or or_1 (or_1_out, and_3_out, and_1_out);
  not not_1 (not_1_out, hour_msb_right);
  and and_3 (and_3_out, not_3_out, not_5_out, out_3, not_9_out, not_7_out, not_10_out, out_8, not_4_out);
  T_Flip_Flop #(.trigger("falling")) t_ff_2 (
    .clk(and_1_out), .T(1'b1), .Q(hour_msb_left), .reset(or_2_out));  // open: Qn, preset, en
  or or_2 (or_2_out, and_3_out, and_2_out);
  not not_2 (not_2_out, hour_msb_left);
  not not_3 (not_3_out, hour_msb_right);
  not not_4 (not_4_out, hour_msb_left);
  T_Flip_Flop #(.trigger("falling")) t_ff_3 (
    .clk(in_1), .T(hour_msb_right), .Q(out_4), .reset(or_3_out));  // open: Qn, preset, en
  or or_3 (or_3_out, and_3_out, and_1_out);
  not not_5 (not_5_out, out_4);
  T_Flip_Flop #(.trigger("falling")) t_ff_4 (
    .clk(and_1_out), .T(hour_msb_left), .Q(out_8), .reset(or_2_out));  // open: Qn, preset, en
  and and_4 (and_4_out, out_4, hour_msb_right);
  and and_5 (and_5_out, out_8, hour_msb_left);
  T_Flip_Flop #(.trigger("falling")) t_ff_5 (
    .clk(in_1), .T(and_4_out), .Q(out_3), .reset(or_3_out));  // open: Qn, preset, en
  T_Flip_Flop #(.trigger("falling")) t_ff_6 (
    .clk(and_1_out), .T(and_5_out), .Q(out_7), .reset(or_2_out));  // open: Qn, preset, en
  not not_6 (not_6_out, out_3);
  not not_7 (not_7_out, out_7);
  and and_6 (and_6_out, out_3, and_4_out);
  and and_7 (and_7_out, out_7, and_5_out);
  T_Flip_Flop #(.trigger("falling")) t_ff_7 (
    .clk(in_1), .T(and_6_out), .Q(hour_lsb_right), .reset(or_3_out));  // open: Qn, preset, en
  T_Flip_Flop #(.trigger("falling")) t_ff_8 (
    .clk(and_1_out), .T(and_7_out), .Q(hour_lsb_left), .reset(or_2_out));  // open: Qn, preset, en
  not not_8 (not_8_out, hour_lsb_left);
  not not_9 (not_9_out, hour_lsb_right);
  not not_10 (not_10_out, hour_lsb_left);

  // Notes on the sheet:
  //   2107080
endmodule

module _7_Segment (
  input  in_1,
  input  in_2,
  input  in_3,
  input  in_4,
  output A,
  output B,
  output C,
  output D,
  output E,
  output F,
  output G
);

  LED_A led_a_1 (.A(in_1), .B(in_2), .C(in_3), .D(in_4), .out_5(A));
  LED_B led_b_1 (.A(in_1), .B(in_2), .C(in_3), .D(in_4), .out_5(B));
  LED_C led_c_1 (.A(in_1), .B(in_2), .C(in_3), .D(in_4), .out_5(C));
  LED_D led_d_1 (.A(in_1), .B(in_2), .C(in_3), .D(in_4), .out_5(D));
  LED_E led_e_1 (.A(in_1), .B(in_2), .C(in_3), .D(in_4), .out_5(E));
  LED_F led_f_1 (.A(in_1), .B(in_2), .C(in_3), .D(in_4), .out_5(F));
  LED_G led_g_1 (.A(in_1), .B(in_2), .C(in_3), .D(in_4), .out_5(G));

  // Notes on the sheet:
  //   2107080
endmodule

module LED_A (
  input  A,
  input  B,
  input  C,
  input  D,
  output out_5
);

  wire A_B_prime_out, A_prime_BD_out, A_prime_D_prime_B_C_out, A_prime_D_prime_B_out, AB_prime_C_prime_out,
       D_prime_A_B_prime_out, not_1_out, not_2_out, not_3_out, not_4_out;

  not not_1 (not_1_out, A);
  not not_2 (not_2_out, B);
  not not_3 (not_3_out, C);
  not not_4 (not_4_out, D);
  or A_prime_D_prime_B (A_prime_D_prime_B_out, not_1_out, not_4_out, B);
  or A_B_prime (A_B_prime_out, A, not_2_out);
  and AB_prime_C_prime (AB_prime_C_prime_out, A, not_2_out, not_3_out);
  and A_prime_BD (A_prime_BD_out, not_1_out, B, D);
  and A_prime_D_prime_B_C (A_prime_D_prime_B_C_out, A_prime_D_prime_B_out, C);
  and D_prime_A_B_prime (D_prime_A_B_prime_out, A_B_prime_out, not_4_out);
  or LED_A (out_5, AB_prime_C_prime_out, A_prime_D_prime_B_C_out, D_prime_A_B_prime_out, A_prime_BD_out);

  // Notes on the sheet:
  //   2107080
endmodule

module LED_B (
  input  A,
  input  B,
  input  C,
  input  D,
  output out_5
);

  wire A_prime_CD__prime_out, A_prime_D_prime_out, AC_prime_D_out, B_prime_A_prime_D_prime_out,
       CD__prime_out, not_1_out, not_2_out, not_3_out, not_4_out;

  not not_1 (not_1_out, A);
  not not_2 (not_2_out, B);
  not not_3 (not_3_out, C);
  not not_4 (not_4_out, D);
  or A_prime_D_prime (A_prime_D_prime_out, not_1_out, not_4_out);
  xnor CD__prime (CD__prime_out, C, D);
  and AC_prime_D (AC_prime_D_out, A, not_3_out, D);
  and B_prime_A_prime_D_prime (B_prime_A_prime_D_prime_out, A_prime_D_prime_out, not_2_out);
  and A_prime_CD__prime (A_prime_CD__prime_out, CD__prime_out, not_1_out);
  or LED_B (out_5, AC_prime_D_out, B_prime_A_prime_D_prime_out, A_prime_CD__prime_out);

  // Notes on the sheet:
  //   2107080
endmodule

module LED_C (
  input  A,
  input  B,
  input  C,
  input  D,
  output out_5
);

  wire A_B_out, B_prime_C_prime_D_out, C_prime_D_2_out, C_prime_D_out, not_1_out, not_2_out;

  not not_1 (not_1_out, B);
  not not_2 (not_2_out, C);
  or C_prime_D (C_prime_D_out, not_2_out, D);
  xor A_B (A_B_out, A, B);
  and B_prime_C_prime_D (B_prime_C_prime_D_out, C_prime_D_out, not_1_out);
  and C_prime_D_2 (C_prime_D_2_out, not_2_out, D);
  or LED_C (out_5, B_prime_C_prime_D_out, A_B_out, C_prime_D_2_out);

  // Notes on the sheet:
  //   2107080
endmodule

module LED_D (
  input  A,
  input  B,
  input  C,
  input  D,
  output out_5
);

  wire A_prime_B_prime_C_out, B_C__prime_D_prime_out, B_C__prime_out, B_prime_D_C_prime_A_out,
       B_prime_D_C_prime_out, B_prime_D_out, BC_prime_D_out, not_1_out, not_2_out, not_3_out, not_4_out;

  not not_1 (not_1_out, A);
  not not_2 (not_2_out, B);
  not not_3 (not_3_out, C);
  not not_4 (not_4_out, D);
  xnor B_C__prime (B_C__prime_out, B, C);
  and A_prime_B_prime_C (A_prime_B_prime_C_out, not_1_out, not_2_out, C);
  and BC_prime_D (BC_prime_D_out, not_3_out, B, D);
  and B_C__prime_D_prime (B_C__prime_D_prime_out, not_4_out, B_C__prime_out);
  and B_prime_D (B_prime_D_out, not_2_out, D);
  or B_prime_D_C_prime (B_prime_D_C_prime_out, B_prime_D_out, not_3_out);
  or LED_D (out_5, A_prime_B_prime_C_out, BC_prime_D_out, B_C__prime_D_prime_out, B_prime_D_C_prime_A_out);
  and B_prime_D_C_prime_A (B_prime_D_C_prime_A_out, B_prime_D_C_prime_out, A);
endmodule

module LED_E (
  input  A,
  input  B,
  input  C,
  input  D,
  output out_5
);

  wire A_B_C_out, B_C_out, B_prime_C_out, D_prime_B_prime_C_out, not_1_out, not_2_out;

  not not_1 (not_1_out, B);
  not not_2 (not_2_out, D);
  or B_C (B_C_out, B, C);
  or B_prime_C (B_prime_C_out, not_1_out, C);
  and A_B_C (A_B_C_out, B_C_out, A);
  and D_prime_B_prime_C (D_prime_B_prime_C_out, B_prime_C_out, not_2_out);
  or LED_E (out_5, A_B_C_out, D_prime_B_prime_C_out);

  // Notes on the sheet:
  //   2107080
endmodule

module LED_F (
  input  A,
  input  B,
  input  C,
  input  D,
  output out_5
);

  wire A_B_prime_C_out, A_prime_BC_prime_out, B_C_prime_out, B_prime_C_out, D_B_C_prime_out, not_1_out,
       not_2_out, not_3_out, not_4_out;

  not not_1 (not_1_out, A);
  not not_2 (not_2_out, B);
  not not_3 (not_3_out, C);
  not not_4 (not_4_out, D);
  or B_prime_C (B_prime_C_out, not_2_out, C);
  or B_C_prime (B_C_prime_out, B, not_3_out);
  and A_prime_BC_prime (A_prime_BC_prime_out, not_1_out, B, not_3_out);
  and A_B_prime_C (A_B_prime_C_out, B_prime_C_out, A);
  and D_B_C_prime (D_B_C_prime_out, B_C_prime_out, not_4_out);
  or LED_F (out_5, A_prime_BC_prime_out, A_B_prime_C_out, D_B_C_prime_out);

  // Notes on the sheet:
  //   2107080
endmodule

module LED_G (
  input  A,
  input  B,
  input  C,
  input  D,
  output out_5
);

  wire A_B_prime_D_out, A_prime_BC_prime_out, B_prime_D_out, B_prime_D_prime_out, C_B_prime_D_prime_out,
       not_1_out, not_2_out, not_3_out, not_4_out;

  not not_1 (not_1_out, A);
  not not_2 (not_2_out, B);
  not not_3 (not_3_out, C);
  not not_4 (not_4_out, D);
  or B_prime_D_prime (B_prime_D_prime_out, not_2_out, not_4_out);
  or B_prime_D (B_prime_D_out, not_2_out, D);
  and C_B_prime_D_prime (C_B_prime_D_prime_out, B_prime_D_prime_out, C);
  and A_prime_BC_prime (A_prime_BC_prime_out, not_1_out, B, not_3_out);
  and A_B_prime_D (A_B_prime_D_out, B_prime_D_out, A);
  or LED_G (out_5, A_prime_BC_prime_out, A_B_prime_D_out, C_B_prime_D_prime_out);

  // Notes on the sheet:
  //   2107080
endmodule
